# Fritzing sketch Mission_4 (saved by Fritzing 0.9.1b)
breadboards: 1

parts:
  LCD1 = LCD screen
  Part1 = Arduino Uno (Rev3)
  Part2 = Bluetooth HC-05
  R2 = Photocell (LDR) [package=THT]
  R3 = Resistor [tolerance=±5% resistance=220 package="0603 [SMD]"]
  R4 = Resistor [tolerance=±5% resistance=220 package=THT]

nets:
  GND: LCD1.VSS, LCD1.R/W, LCD1.LED-, Part1.GND, Part2.RXD, Part2.GND, R3.Pin_0, R4.Pin_1
  VDD: LCD1.VDD, LCD1.V0, LCD1.LED+, Part1.5V, Part2.VCC, R2.pin_1
  N1: LCD1.RS, Part1.D12/MISO
  N2: LCD1.E, Part1.D11_PWM/MOSI
  N3: LCD1.DB4, Part1.D2
  N4: LCD1.DB5, Part1.D3_PWM
  N5: LCD1.DB6, Part1.D4
  N6: LCD1.DB7, Part1.D5_PWM
  N7: Part1.A0, R2.pin_0, R3.Pin_1
  N8: Part1.D0/RX, Part2.TXD
  N9: Part1.D1/TX, R4.Pin_0
