# Fritzing sketch Mission_4 (saved by Fritzing 0.9.1b)
breadboards: 1

parts:
  LED1 = LED - 5mm [color="Red (633nm)" package="5 mm [THT]"]
  LED2 = LED - 5mm [color="Red (633nm)" package="5 mm [THT]"]
  LED3 = LED - 5mm [color="Red (633nm)" package="5 mm [THT]"]
  LED4 = LED - 5mm [color="Red (633nm)" package="5 mm [THT]"]
  R1 = Resistor [tolerance=±5% resistance=220 package=THT]
  R2 = Resistor [tolerance=±5% resistance=220 package=THT]
  R3 = Resistor [tolerance=±5% resistance=220 package=THT]
  R4 = Resistor [tolerance=±5% resistance=220 package=THT]
  S2 = Reed switch [package=THT]
  S3 = Reed switch [package=THT]
  S4 = Reed switch [package=THT]
  J1 = Piezo Speaker
  J2 = Piezo Speaker
  J3 = Piezo Speaker
  J4 = Piezo Speaker
  VCC1 = Battery

nets:
  N1: LED1.cathode, S4.pin_2
  N2: LED1.anode, R1.Pin_0
  N3: LED2.cathode, S3.pin_2
  N4: LED2.anode, R2.Pin_0
  N5: LED3.cathode, S2.pin_2
  N6: LED3.anode, R3.Pin_0
  N7: LED4.anode, R4.Pin_0
  N8: R1.Pin_1, R2.Pin_1, R3.Pin_1, R4.Pin_1, VCC1.+
  N9: S2.pin_1, J3.pin2
  N10: S3.pin_1, J2.pin2
  N11: S4.pin_1, J1.pin2
  N12: J1.pin1, J2.pin1, J3.pin1, J4.pin1
